# Fritzing sketch shema MQ 2 (saved by Fritzing 0.9.3b)
circuit board: 8.46667cm x 5.64444cm
breadboards: 1

parts:
  Част1 = MQ-3 breakout
  Част2 = Arduino Nano (Rev3.0)
  J1 = Piezo Speaker
  LED1 = LED - 5mm [color="Red (633nm)" package="5 mm [THT]"]
  LED2 = LED - 5mm [color="Green (565nm)" package="5 mm [THT]"]
  R1 = Resistor [tolerance=±5% resistance=220 package="0402 [SMD]"]
  R2 = Resistor [tolerance=±5% resistance=220 package="0402 [SMD]"]
  R3 = Resistor [tolerance=±5% resistance=220 package="0402 [SMD]"]

nets:
  VCC: Част1.VCC, Част2.5V
  GND: Част1.GND, Част2.GND, R1.Pin_1, R2.Pin_1, R3.Pin_1
  N1: Част1.AO, Част2.A5
  N2: Част2.D10, J1.pin2
  N3: Част2.D11/MOSI, LED2.anode
  N4: Част2.D12/MISO, LED1.anode
  N5: J1.pin1, R3.Pin_0
  N6: LED1.cathode, R1.Pin_0
  N7: LED2.cathode, R2.Pin_0

notes:
  MQ-2,3,4...
  Vcc GND D0 A0
  GND
  +5 V
  D10
  D11
  D12

custom parts:
  MQ-3 breakout: Alcohol sensor is capable of detecting alcohol (ethanol) particles on itself and gives the information in digital form back to us to manipulate with it. SKU:101251 • Voltage: 5V DC • Power: max 750mW • Measurement range: 0.04-4mg/L
